// Digital circuit project.dig as structural Verilog
module project (
  input  in_1,
  input  clk,
  output [6:0] out_3,
  output [15:0] out_4
);

  wire _0_out, _1_out, _2_out, _3_out, _4_out, _5_out, _6_out, _7_out, _8_out, _9_out, and_1_out, and_2_out,
       ID_2_out, mode_selector_1_ido, mode_selector_1_pwdo, PASS_2_out, shifter_pwd_1_led1,
       shifter_pwd_1_led2, shifter_pwd_1_led3, shifter_pwd_1_led4, shifter_pwd_1_match, u_encoder_da,
       u_timer_dis, u_timer_reset;
  wire [3:0] shifter_1_id0, shifter_1_id1, u_encoder_data;

  Button _1 (.out(_1_out));
  Button _4 (.out(_4_out));
  Button _7 (.out(_7_out));
  Button _2 (.out(_2_out));
  Button _5 (.out(_5_out));
  Button _8 (.out(_8_out));
  Button _0 (.out(_0_out));
  Button _3 (.out(_3_out));
  Button _6 (.out(_6_out));
  Button _9 (.out(_9_out));
  LED ID (.in(mode_selector_1_ido));
  LED PASS (.in(mode_selector_1_pwdo));
  Button ID_2 (.out(ID_2_out));
  Button PASS_2 (.out(PASS_2_out));
  mode_selector mode_selector_1 (
    .ID(ID_2_out), .PWD(PASS_2_out), .DIS(u_timer_dis), .RESET(u_timer_reset), .CLK(clk), .RST(in_1),
    .IDO(mode_selector_1_ido), .PWDO(mode_selector_1_pwdo));
  encoder #(.applicationType("IVERILOG")) u_encoder (
    .P0(_0_out), .P1(_1_out), .P2(_2_out), .P3(_3_out), .P4(_4_out), .P5(_5_out), .P6(_6_out), .P7(_7_out),
    .P8(_8_out), .P9(_9_out), .CLK(clk), .RST(in_1), .DATA(u_encoder_data), .DA(u_encoder_da));
  ROM #(.AddrBits(7), .Bits(16)) Password (.A(out_3), .sel(1'b1), .D(out_4));
  timer #(.applicationType("IVERILOG")) u_timer (
    .start(shifter_pwd_1_led4), .clk(clk), .rst(in_1), .reset(u_timer_reset), .dis(u_timer_dis));
  shifter shifter_1 (
    .IN(u_encoder_data), .EN(mode_selector_1_ido), .DA(u_encoder_da), .CLK(clk), .RST(in_1),
    .ID1(shifter_1_id1), .ID0(shifter_1_id0), .HEX(out_3));
  shifter_pwd shifter_pwd_1 (
    .DATA_in(u_encoder_data), .PWD_in(out_4), .EN(mode_selector_1_pwdo), .DA(u_encoder_da), .CLK(clk),
    .RST(in_1), .MATCH(shifter_pwd_1_match), .LED1(shifter_pwd_1_led1), .LED2(shifter_pwd_1_led2),
    .LED3(shifter_pwd_1_led3), .LED4(shifter_pwd_1_led4));
  Seven_Seg_Hex seven_seg_hex_1 (.d(shifter_1_id1), .dp(1'b0));
  Seven_Seg_Hex seven_seg_hex_2 (.d(shifter_1_id0), .dp(1'b0));
  LED led_1 (.in(shifter_pwd_1_led1));
  LED led_2 (.in(shifter_pwd_1_led2));
  and and_1 (and_1_out, shifter_pwd_1_match, shifter_pwd_1_led4);
  and and_2 (and_2_out, ~shifter_pwd_1_match, shifter_pwd_1_led4);  // And
  LED led_3 (.in(shifter_pwd_1_led3));
  LED led_4 (.in(shifter_pwd_1_led4));
  LED GRANTED (.in(and_1_out));
  LED DENIED (.in(and_2_out));

  // Notes on the sheet:
  //   clk: Hz: 100
  //   Zeynep Türkmen - 29541,
  //   Emre Kaan Usta - 30728
  //   contents of Password (hex, n*v repeats v):
  //   4d2,162e,270f,0,31*ffff,1919,63*ffff
endmodule

/* Code of encoder:
module encoder(
	input P0, P1, P2, P3, P4, P5, P6, P7, P8, P9,
	input CLK, RST,
	output reg [3:0] DATA,
	output reg DA);
	
	reg pressed;
	wire button;

	assign button = P0|P1|P2|P3|P4|P5|P6|P7|P8|P9;

	always @(posedge CLK, negedge RST) 
		if(~RST)
		begin
			pressed <= 0;
			DATA <= 4'b0000;
		end
		else
		begin
			if(button)
			begin
				if(~pressed)
				begin
					pressed <= 1'b1;
					DA <= 1'b1;
				end
				else
					DA <= 1'b0;
				if      (P0) DATA <= 4'b0000;
				else if (P1) DATA <= 4'b0001;
				else if (P2) DATA <= 4'b0010;
				else if (P3) DATA <= 4'b0011;
				else if (P4) DATA <= 4'b0100;
				else if (P5) DATA <= 4'b0101;
				else if (P6) DATA <= 4'b0110;
				else if (P7) DATA <= 4'b0111;
				else if (P8) DATA <= 4'b1000;
				else         DATA <= 4'b1001;
			end
			else
			begin
				pressed <= 1'b0;
				DA <= 1'b0;
			end				
		end			
endmodule
*/

/* Code of timer:
module timer(
   input start, clk, rst,
   output reg reset,
   output reg dis);

   reg state;
   reg [8:0] CNT;
   
   parameter IDLE = 1'b0, COUNT = 1'b1, LIMIT = 8'd220;
   
   wire timeup;

   assign timeup = (CNT == LIMIT);

   // Sequential part
   always @(posedge clk or negedge rst) begin
     if (!rst) begin
       state <= IDLE;
       reset <= 1'b0;
       CNT <= 0;
     end else begin
       case(state)
         IDLE:
           begin
             CNT <= 0;
	     reset <= 1'b0;
             if (start)begin
	       dis <= 1'b1;
               state <= COUNT; end
             else begin
	       dis <= 1'b0;
               state <= IDLE;end
           end
         COUNT:
           begin
             CNT <= CNT + 1;
             if (timeup)begin
	       dis <= 1'b0;
	       reset <= 1'b1;
               state <= IDLE;end
             else begin
	       dis <= 1'b1;	
               state <= COUNT; end
           end
         default:
           begin
             CNT <= CNT;
             state <= IDLE;
           end
       endcase // case (state)
     end
   end

endmodule // timerTest
*/
