// Digital circuit shifter.dig as structural Verilog
module shifter (
  input  [3:0] IN,
  input  EN,
  input  DA,
  input  CLK,
  input  RST,
  output [3:0] ID1,
  output [3:0] ID0,
  output [6:0] HEX
);

  wire add_1_c_o, and_1_out, not_1_out;
  wire [3:0] multiplexer_1_out, multiplexer_2_out;
  wire [7:0] mul_1_mul;
  wire [7:7] add_1_s;

  and and_1 (and_1_out, EN, DA);
  not not_1 (not_1_out, RST);
  Mul #(.Bits(4)) mul_1 (.a(4'b1010), .b(ID1), .mul(mul_1_mul));
  Add #(.Bits(8)) add_1 (.a({4'b0000, ID0}), .b(mul_1_mul), .c_i(1'b0), .s({add_1_s[7], HEX}), .c_o(add_1_c_o));
  D_FF_AS #(.Bits(4)) MSB (.Set(1'b0), .D(multiplexer_1_out), .C(CLK), .Clr(not_1_out), .Q(ID1));  // open: nQ
  Multiplexer #(.Bits(4)) multiplexer_1 (.sel(and_1_out), .in_0(ID1), .in_1(ID0), .out(multiplexer_1_out));
  D_FF_AS #(.Bits(4)) LSB (.Set(1'b0), .D(multiplexer_2_out), .C(CLK), .Clr(not_1_out), .Q(ID0));  // open: nQ
  Multiplexer #(.Bits(4)) multiplexer_2 (.sel(and_1_out), .in_0(ID0), .in_1(IN), .out(multiplexer_2_out));

  // Notes on the sheet:
  //   Zeynep Türkmen - 29541,
  //   Emre Kaan Usta - 30728
endmodule
