// Digital circuit timer.dig as structural Verilog
module timer (
  input  START,
  input  CLK,
  input  RST,
  output RESET,
  output DIS
);

  wire and_1_out, and_2_out, and_3_out, and_4_out, d_ff_as_1_nq, not_1_out, not_2_out, not_3_out, not_4_out,
       or_1_out, or_2_out, or_3_out;
  wire [1:0] jk_ff_as_1_q;

  not not_1 (not_1_out, RST);
  not not_2 (not_2_out, RESET);
  and and_1 (and_1_out, d_ff_as_1_nq, START);
  and and_2 (and_2_out, DIS, not_2_out);
  or or_1 (or_1_out, and_1_out, and_2_out);
  D_FF_AS d_ff_as_1 (.Set(1'b0), .D(or_1_out), .C(CLK), .Clr(not_1_out), .Q(DIS), .nQ(d_ff_as_1_nq));
  not not_3 (not_3_out, d_ff_as_1_nq);
  and and_3 (and_3_out, DIS, not_3_out);
  not not_4 (not_4_out, not_3_out);
  and and_4 (and_4_out, jk_ff_as_1_q[0], and_3_out);
  or or_2 (or_2_out, and_3_out, not_4_out);
  or or_3 (or_3_out, and_4_out, not_4_out);
  JK_FF_AS jk_ff_as_1 (
    .Set(1'b0), .J(and_3_out), .C(CLK), .K(or_2_out), .Clr(not_1_out), .Q(jk_ff_as_1_q[0]));  // open: nQ
  JK_FF_AS jk_ff_as_2 (
    .Set(1'b0), .J(and_4_out), .C(CLK), .K(or_3_out), .Clr(not_1_out), .Q(jk_ff_as_1_q[1]));  // open: nQ
  and and_5 (RESET, jk_ff_as_1_q[0], jk_ff_as_1_q[1]);
  Seven_Seg_Hex seven_seg_hex_1 (.d({2'b00, jk_ff_as_1_q}), .dp(1'b0));
endmodule
